# Fritzing sketch shield (saved by Fritzing 0.9.3b)
breadboards: 2

parts:
  Part2 = Arduino Pro Mini (5V)
  Part3 = Bluetooth HC-05 Macho
  Part4 = Tri-Axis Gyro Breakout - L3G4200D
  R1 = Resistor [tolerance=±5% resistance=1k package=THT]
  R2 = Resistor [tolerance=±5% resistance=2k package=THT]
  Part5 = Thumb Joystick
  S1 = Pushbutton [package="[SMD]"]
  S2 = Pushbutton [package="[SMD]"]
  S3 = Pushbutton [package="[SMD]"]
  S4 = Pushbutton [package="[SMD]"]
  U1 = LIPO-2000mAh [package=lipo-2000]

nets:
  N1: Part2.A4, Part4.SDA
  N2: Part2.A5, Part4.SCL
  N3: Part3.RXD, R1.Pin_1, R2.Pin_0
  GND: Part4.GND, R2.Pin_1, Part5.GND, S1.Pin_3, S1.Pin_4, S2.Pin_3, S2.Pin_4, S3.Pin_3, S3.Pin_4, S4.Pin_3, S4.Pin_4, U1.-
  VCC: Part4.VCC, Part5.VCC
  N4: S1.Pin_1, S1.Pin_2
  N5: S2.Pin_1, S2.Pin_2
  N6: S3.Pin_1, S3.Pin_2
  N7: S4.Pin_1, S4.Pin_2

notes:
  you should supply the arduino with 5v
  I used an arduino pro mini but you can use any arduino as long as you connect the same pins
  dropping the voltage from 5v to 3.3v using a voltage divider (1k to arduino TX 2k to ground)
