# Fritzing sketch sword (saved by Fritzing 0.9.3b)
breadboards: 2

parts:
  Part1 = Arduino Uno (Rev3) - ICSP
  Part2 = IMU Digital Combo Board 6DOF
  Part3 = Thumb Joystick
  Part4 = Bluetooth HC-05 Macho
  Part5 = Bluetooth HC-05 Macho
  U2 = BATTERY-2 [package=battery-aa]
  U3 = BATTERY-2 [package=battery-aa]
  U4 = BATTERY-2 [package=battery-aa]
  U5 = BATTERY-2 [package=battery-aa]
  S2 = Momentary Switch [package=ksa_sealed_tac_switch]
  S3 = Pushbutton [package="[SMD]"]
  S4 = Pushbutton [package="[SMD]"]
  S5 = Pushbutton [package="[SMD]"]
  S6 = Pushbutton [package="[THT]"]
  R1 = Resistor [tolerance=±5% resistance=2.2k package="1206 [SMD]"]
  R2 = Resistor [tolerance=±5% resistance=2.2k package="1206 [SMD]"]
  R3 = Resistor [tolerance=±5% resistance=220 package="1206 [SMD]"]
  R4 = Resistor [tolerance=±5% resistance=220 package="1206 [SMD]"]
  S1 = SWITCH-DPDT [package=ayz0202]

nets:
  N1: Part1.A2, Part3.VERT
  N2: Part1.A3, Part3.HORZ
  N3: Part1.A4/SDA, Part2.SDA
  N4: Part1.A5/SCL, Part2.SCL
  N5: Part1.D8, S5.Pin_1, S5.Pin_2
  N6: Part1.D9_PWM, Part3.SEL
  N7: Part1.D10_PWM/SS, S6.Pin_1, S6.Pin_2
  N8: Part1.D0/RX, Part5.TXD
  N9: Part1.D1/TX, R4.Pin_0
  N10: Part1.D2, Part4.TXD
  N11: Part1.D3_PWM, R3.Pin_0
  N12: Part1.D5_PWM, S3.Pin_1, S3.Pin_2
  N13: Part1.D6_PWM, S2.2
  N14: Part1.D7, S4.Pin_1, S4.Pin_2
  VCC: Part1.5V, Part2.3.3V, Part3.VCC, Part4.VCC, Part5.VCC
  GND: Part1.GND, Part2.GND, Part3.GND, Part4.GND, Part5.GND, S2.3, S3.Pin_3, S3.Pin_4, S5.Pin_3, S5.Pin_4, S6.Pin_3, S6.Pin_4, R1.Pin_1, R2.Pin_1, S1.3
  N15: Part1.VIN, S1.4
  N16: Part4.RXD, R2.Pin_0, R3.Pin_1
  N17: Part5.RXD, R1.Pin_0, R4.Pin_1
  N18: U2.-1, S1.1
  N19: U2.+1, U3.-1
  N20: U3.+1, U5.-1
  N21: U4.-1, U5.+1
  N22: U4.+1, S1.6
  N23: S2.4, S4.Pin_3, S4.Pin_4

notes:
  this is a placeholder for the MPU6050 but the connections are the same
  I used a voltage divider on the RX pins(2K resistor to ground 1K to arduino RX) because the arduino sends 5v signals but the hc05 should take in 3.3v
  you can replace the batteries with any other 5v power supply

// code stored in the sketch: sword.ino

